// Logisim project circuito parcial 2.circ as structural Verilog: 3 circuits, main circuit Parcial 2
module Parcial_2 (
  input  Reset
);

  wire adder_2_cout, uc_1_hin, uc_1_hout, uc_1_jin, uc_1_jout, uc_1_memrw, uc_1_pcin, uc_1_selbusc,
       uc_1_selbusdir, uc_1_sync;
  wire [3:0] adder_1_out, multiplexer_2_out, register_1_q, uc_1_posmemoria;
  wire [7:0] adder_2_out, controlled_buffer_1_out, multiplexer_1_out, register_2_q, register_3_q;

  Multiplexer #(.select(1), .width(8)) multiplexer_1 (
    .in0(adder_2_out), .in1(controlled_buffer_1_out), .out(multiplexer_1_out), .sel(uc_1_selbusc));
  Register #(.width(4), .trigger("rising")) register_1 (
    .D(adder_1_out), .Q(register_1_q), .clk(uc_1_pcin), .clr(Reset));  // open: en
  Register #(.width(8), .trigger("high")) register_2 (
    .D(multiplexer_1_out), .Q(register_2_q), .clk(uc_1_hin));  // open: en, clr
  Register #(.width(8), .trigger("high")) register_3 (
    .D(multiplexer_1_out), .Q(register_3_q), .clk(uc_1_jin), .clr(Reset));  // open: en
  Adder #(.width(4)) adder_1 (.a(4'b0001), .b(register_1_q), .out(adder_1_out));  // open: cin, cout
  Adder #(.width(8)) adder_2 (.a(register_2_q), .b(register_3_q), .out(adder_2_out), .cout(adder_2_cout));  // open: cin
  UC uc_1 (
    .PCin(uc_1_pcin), .Hin(uc_1_hin), .Jin(uc_1_jin), .SelBusC(uc_1_selbusc), .PosMemoria(uc_1_posmemoria),
    .IR(controlled_buffer_1_out), .SelBusDir(uc_1_selbusdir), .MemRW(uc_1_memrw), .Hout(uc_1_hout),
    .Jout(uc_1_jout), .sync(uc_1_sync));
  assign controlled_buffer_1_out = uc_1_hout ? register_2_q : 8'bz;  // Controlled_Buffer controlled_buffer_1
  assign controlled_buffer_1_out = uc_1_jout ? register_3_q : 8'bz;  // Controlled_Buffer controlled_buffer_2
  Multiplexer #(.select(1), .width(4)) multiplexer_2 (
    .in0(register_1_q), .in1(uc_1_posmemoria), .out(multiplexer_2_out), .sel(uc_1_selbusdir));
  RAM #(.addrWidth(4), .dataWidth(8), .bus("combined")) ram_1 (
    .addr(multiplexer_2_out), .data(controlled_buffer_1_out), .clk(uc_1_sync), .ld(uc_1_memrw));  // open: sel, clr

  // Notes on the sheet:
  //   Bus C
  //   PC
  //   H
  //   J
  //   Bus B
  //   Bus A
  //   Incrementador de PC
  //   PCin
  //   Hin
  //   Jin
  //   SelBusC
  //   ALU
  //   C
  //   N
  //   V
  //   PosMemoria
  //   IR
  //   UC
  //   Hout
  //   Jout
  //   Z
  //   Bus de direcciones
  //   SelBusDir
  //   MemRW
  //   Bus de datos
endmodule

module UC (
  input  [7:0] IR,
  output [3:0] PosMemoria,
  output PCin,
  output SelBusDir,
  output Hin,
  output MemRW,
  output Jin,
  output Hout,
  output SelBusC,
  output Jout,
  output sync
);

  wire clock_1_out;
  wire [1:0] rom_1_data;
  wire [3:0] register_1_q;
  wire [4:0] adder_1_out, multiplexer_1_out, register_2_q;
  wire [9:2] rom_1_data_2;

  Adder #(.width(5)) adder_1 (.a(register_2_q), .b(5'b00001), .out(adder_1_out));  // open: cin, cout
  Multiplexer #(.select(2), .width(5)) multiplexer_1 (
    .in0(adder_1_out), .in1({1'b1, register_1_q[3:2], 2'b00}), .in2({5{1'b0}}), .out(multiplexer_1_out),
    .sel(rom_1_data));  // open: in3
  Register #(.width(8), .trigger("high")) register_1 (
    .D(IR), .Q({register_1_q, PosMemoria}), .clk(rom_1_data_2[9]));  // open: en, clr
  Register #(.width(5), .trigger("rising")) register_2 (
    .D(multiplexer_1_out), .Q(register_2_q), .clk(clock_1_out));  // open: en, clr
  Clock #(.highDuration(1), .lowDuration(1)) clock_1 (.out(clock_1_out));
  ROM #(.addrWidth(5), .dataWidth(10)) rom_1 (
    .addr(register_2_q),
    .data({rom_1_data_2[9], PCin, SelBusDir, SelBusC, MemRW, sync, rom_1_data_2[3:2], rom_1_data}));  // open: sel
  regDecode regdecode_1 (.in_1(register_1_q[1]), .in_2(rom_1_data_2[3]), .H(Hin), .J(Jin));
  regDecode regdecode_2 (.in_1(register_1_q[1]), .in_2(rom_1_data_2[2]), .H(Hout), .J(Jout));

  // Notes on the sheet:
  //   contents of rom_1 (hex, n*v repeats v):
  //   230 101 14*0 fa 0 0 0 84 95 0 0 a
endmodule

module regDecode (
  input  in_1,
  input  in_2,
  output H,
  output J
);

  wire decoder_1_out0, decoder_1_out1;

  Decoder #(.select(1), .tristate("false")) decoder_1 (.out0(decoder_1_out0), .out1(decoder_1_out1), .sel(in_1));
  and and_1 (H, in_2, decoder_1_out0);
  and and_2 (J, decoder_1_out1, in_2);
endmodule
