// Logisim project ALU.BAK.circ as structural Verilog: 4 circuits, main circuit ALU
module ALU (
  input  ADD,
  input  AND,
  input  [15:0] Num_1,
  input  [15:0] Num_2,
  output [15:0] Num_1___Num_2,
  output Overflow,
  output Zero
);

  wire and_17_out, and_18_out, not_1_out, not_2_out, or_1_out, or_2_out;
  wire [15:0] adder_1_out, and_1_out;

  Adder #(.width(16)) adder_1 (.a(Num_1), .b(Num_2), .out(adder_1_out), .cout(Overflow));  // open: cin
  not not_1 (not_1_out, ADD);
  not not_2 (not_2_out, AND);
  and and_1 (and_1_out[0], Num_1[0], Num_2[0]);
  and and_2 (and_1_out[1], Num_1[1], Num_2[1]);
  and and_3 (and_1_out[2], Num_1[2], Num_2[2]);
  and and_4 (and_1_out[3], Num_1[3], Num_2[3]);
  and and_5 (and_1_out[4], Num_1[4], Num_2[4]);
  and and_6 (and_1_out[5], Num_1[5], Num_2[5]);
  and and_7 (and_1_out[6], Num_1[6], Num_2[6]);
  and and_8 (and_1_out[7], Num_1[7], Num_2[7]);
  and and_9 (and_1_out[8], Num_1[8], Num_2[8]);
  and and_10 (and_1_out[9], Num_1[9], Num_2[9]);
  and and_11 (and_1_out[10], Num_1[10], Num_2[10]);
  and and_12 (and_1_out[11], Num_1[11], Num_2[11]);
  and and_13 (and_1_out[12], Num_1[12], Num_2[12]);
  and and_14 (and_1_out[13], Num_1[13], Num_2[13]);
  and and_15 (and_1_out[14], Num_1[14], Num_2[14]);
  and and_16 (and_1_out[15], Num_1[15], Num_2[15]);
  and and_17 (and_17_out, not_2_out, ADD);
  and and_18 (and_18_out, AND, not_1_out);
  assign Num_1___Num_2 = and_17_out ? adder_1_out : 16'bz;  // Controlled_Buffer controlled_buffer_1
  assign Num_1___Num_2 = and_18_out ? and_1_out : 16'bz;  // Controlled_Buffer controlled_buffer_2
  or or_1 (or_1_out, Num_1___Num_2[0], Num_1___Num_2[1], Num_1___Num_2[2], Num_1___Num_2[3], Num_1___Num_2[4], Num_1___Num_2[5], Num_1___Num_2[6], Num_1___Num_2[7], Num_1___Num_2[8]);
  or or_2 (or_2_out, Num_1___Num_2[9], Num_1___Num_2[10], Num_1___Num_2[11], Num_1___Num_2[12], Num_1___Num_2[13], Num_1___Num_2[14], Num_1___Num_2[15]);
  nor nor_1 (Zero, or_1_out, or_2_out);

  // Notes on the sheet:
  //   Sergio Botero Uribe 20092
endmodule

module ALU2 (
  input  JZ,
  input  _0_AND_1_ADD,
  input  [15:0] Num_1,
  input  [15:0] Num_2,
  input  [15:0] in_5,
  output [15:0] Num_1___Num_2,
  output Overflow,
  output Zero
);

  wire and_1_out, and_18_out, and_19_out, not_2_out, not_3_out, or_1_out, or_2_out;
  wire [15:0] adder_1_out, adder_2_out, and_2_out, controlled_buffer_1_out, not_1_out;

  assign not_1_out = ~Num_2;  // NOT_Gate not_1, 16 bits wide
  Adder #(.width(16)) adder_1 (.a(not_1_out), .b(in_5), .out(adder_1_out));  // open: cin, cout
  assign controlled_buffer_1_out = not_2_out ? Num_2 : 16'bz;  // Controlled_Buffer controlled_buffer_1
  not not_2 (not_2_out, and_1_out);
  assign controlled_buffer_1_out = and_1_out ? adder_1_out : 16'bz;  // Controlled_Buffer controlled_buffer_2
  and and_1 (and_1_out, JZ, _0_AND_1_ADD);
  Adder #(.width(16)) adder_2 (
    .a(Num_1), .b(controlled_buffer_1_out), .out(adder_2_out), .cout(Overflow));  // open: cin
  not not_3 (not_3_out, _0_AND_1_ADD);
  and and_2 (and_2_out[0], Num_1[0], controlled_buffer_1_out[0]);
  and and_3 (and_2_out[1], Num_1[1], controlled_buffer_1_out[1]);
  and and_4 (and_2_out[2], Num_1[2], controlled_buffer_1_out[2]);
  and and_5 (and_2_out[3], Num_1[3], controlled_buffer_1_out[3]);
  and and_6 (and_2_out[4], Num_1[4], controlled_buffer_1_out[4]);
  and and_7 (and_2_out[5], Num_1[5], controlled_buffer_1_out[5]);
  and and_8 (and_2_out[6], Num_1[6], controlled_buffer_1_out[6]);
  and and_9 (and_2_out[7], Num_1[7], controlled_buffer_1_out[7]);
  and and_10 (and_2_out[8], Num_1[8], controlled_buffer_1_out[8]);
  and and_11 (and_2_out[9], Num_1[9], controlled_buffer_1_out[9]);
  and and_12 (and_2_out[10], Num_1[10], controlled_buffer_1_out[10]);
  and and_13 (and_2_out[11], Num_1[11], controlled_buffer_1_out[11]);
  and and_14 (and_2_out[12], Num_1[12], controlled_buffer_1_out[12]);
  and and_15 (and_2_out[13], Num_1[13], controlled_buffer_1_out[13]);
  and and_16 (and_2_out[14], Num_1[14], controlled_buffer_1_out[14]);
  and and_17 (and_2_out[15], Num_1[15], controlled_buffer_1_out[15]);
  and and_18 (and_18_out, 1'b1, _0_AND_1_ADD);
  and and_19 (and_19_out, 1'b1, not_3_out);
  assign Num_1___Num_2 = and_18_out ? adder_2_out : 16'bz;  // Controlled_Buffer controlled_buffer_3
  assign Num_1___Num_2 = and_19_out ? and_2_out : 16'bz;  // Controlled_Buffer controlled_buffer_4
  or or_1 (or_1_out, Num_1___Num_2[0], Num_1___Num_2[1], Num_1___Num_2[2], Num_1___Num_2[3], Num_1___Num_2[4], Num_1___Num_2[5], Num_1___Num_2[6], Num_1___Num_2[7], Num_1___Num_2[8]);
  or or_2 (or_2_out, Num_1___Num_2[9], Num_1___Num_2[10], Num_1___Num_2[11], Num_1___Num_2[12], Num_1___Num_2[13], Num_1___Num_2[14], Num_1___Num_2[15]);
  nor nor_1 (Zero, or_1_out, or_2_out);

  // Notes on the sheet:
  //   Sergio Botero Uribe 20092
endmodule

module REG (
  input  [15:0] In,
  input  W,
  input  R,
  input  [1:0] Num_Registro,
  output [15:0] Out
);

  wire and_1_out, and_2_out, and_3_out, and_4_out, and_5_out, and_6_out, and_7_out, and_8_out, and_9_out,
       and_10_out, and_11_out, and_12_out, not_1_out, not_2_out, not_3_out, not_4_out;
  wire [15:0] controlled_buffer_1_out, controlled_buffer_3_out, controlled_buffer_6_out,
       controlled_buffer_7_out, Registro_1_q, Registro_2_q, Registro_3_q, Registro_4_q;

  assign controlled_buffer_1_out = and_1_out ? In : 16'bz;  // Controlled_Buffer controlled_buffer_1
  and and_1 (and_1_out, W, and_2_out);
  and and_2 (and_2_out, not_2_out, not_1_out);
  not not_1 (not_1_out, Num_Registro[1]);
  not not_2 (not_2_out, Num_Registro[0]);
  assign Out = and_3_out ? Registro_1_q : 16'bz;  // Controlled_Buffer controlled_buffer_2
  Register #(.width(16), .trigger("high")) Registro_1 (
    .D(controlled_buffer_1_out), .Q(Registro_1_q), .clk(and_1_out));  // open: en, clr
  and and_3 (and_3_out, and_2_out, R);
  assign controlled_buffer_3_out = and_4_out ? In : 16'bz;  // Controlled_Buffer controlled_buffer_3
  and and_4 (and_4_out, W, and_5_out);
  and and_5 (and_5_out, Num_Registro[0], not_3_out);
  not not_3 (not_3_out, Num_Registro[1]);
  assign Out = and_6_out ? Registro_2_q : 16'bz;  // Controlled_Buffer controlled_buffer_4
  Register #(.width(16), .trigger("high")) Registro_2 (
    .D(controlled_buffer_3_out), .Q(Registro_2_q), .clk(and_4_out));  // open: en, clr
  and and_6 (and_6_out, and_5_out, R);
  assign Out = and_9_out ? Registro_3_q : 16'bz;  // Controlled_Buffer controlled_buffer_5
  Register #(.width(16), .trigger("high")) Registro_3 (
    .D(controlled_buffer_6_out), .Q(Registro_3_q), .clk(and_7_out));  // open: en, clr
  assign controlled_buffer_6_out = and_7_out ? In : 16'bz;  // Controlled_Buffer controlled_buffer_6
  and and_7 (and_7_out, W, and_8_out);
  and and_8 (and_8_out, not_4_out, Num_Registro[1]);
  not not_4 (not_4_out, Num_Registro[0]);
  and and_9 (and_9_out, and_8_out, R);
  assign controlled_buffer_7_out = and_10_out ? In : 16'bz;  // Controlled_Buffer controlled_buffer_7
  and and_10 (and_10_out, W, and_11_out);
  assign Out = and_12_out ? Registro_4_q : 16'bz;  // Controlled_Buffer controlled_buffer_8
  Register #(.width(16), .trigger("high")) Registro_4 (
    .D(controlled_buffer_7_out), .Q(Registro_4_q), .clk(and_10_out));  // open: en, clr
  and and_11 (and_11_out, Num_Registro[0], Num_Registro[1]);
  and and_12 (and_12_out, and_11_out, R);

  // Notes on the sheet:
  //   Sergio Botero Uribe 20092
endmodule

module UC (
);

  wire clock_1_out;

  Clock #(.highDuration(1), .lowDuration(1)) clock_1 (.out(clock_1_out));

  // Notes on the sheet:
  //   Sergio Botero Uribe 20092
endmodule
