// Logisim project ALU.circ as structural Verilog: 6 circuits, main circuit PROC
module ALU (
  input  ADD,
  input  AND,
  input  ALU_SIGNAL,
  input  [15:0] Num_1,
  input  [15:0] Num_2,
  output [15:0] Num_1___Num_2,
  output Overflow,
  output Zero
);

  wire and_17_out, and_18_out, not_1_out, not_2_out, or_1_out, or_2_out;
  wire [15:0] adder_1_out, and_1_out, controlled_buffer_1_out;

  Adder #(.width(16)) adder_1 (.a(Num_1), .b(Num_2), .out(adder_1_out), .cout(Overflow));  // open: cin
  not not_1 (not_1_out, ADD);
  not not_2 (not_2_out, AND);
  and and_1 (and_1_out[0], Num_1[0], Num_2[0]);
  and and_2 (and_1_out[1], Num_1[1], Num_2[1]);
  and and_3 (and_1_out[2], Num_1[2], Num_2[2]);
  and and_4 (and_1_out[3], Num_1[3], Num_2[3]);
  and and_5 (and_1_out[4], Num_1[4], Num_2[4]);
  and and_6 (and_1_out[5], Num_1[5], Num_2[5]);
  and and_7 (and_1_out[6], Num_1[6], Num_2[6]);
  and and_8 (and_1_out[7], Num_1[7], Num_2[7]);
  and and_9 (and_1_out[8], Num_1[8], Num_2[8]);
  and and_10 (and_1_out[9], Num_1[9], Num_2[9]);
  and and_11 (and_1_out[10], Num_1[10], Num_2[10]);
  and and_12 (and_1_out[11], Num_1[11], Num_2[11]);
  and and_13 (and_1_out[12], Num_1[12], Num_2[12]);
  and and_14 (and_1_out[13], Num_1[13], Num_2[13]);
  and and_15 (and_1_out[14], Num_1[14], Num_2[14]);
  and and_16 (and_1_out[15], Num_1[15], Num_2[15]);
  and and_17 (and_17_out, not_2_out, ADD);
  and and_18 (and_18_out, AND, not_1_out);
  assign controlled_buffer_1_out = and_17_out ? adder_1_out : 16'bz;  // Controlled_Buffer controlled_buffer_1
  assign controlled_buffer_1_out = and_18_out ? and_1_out : 16'bz;  // Controlled_Buffer controlled_buffer_2
  assign Num_1___Num_2 = ALU_SIGNAL ? controlled_buffer_1_out : 16'bz;  // Controlled_Buffer controlled_buffer_3
  or or_1 (or_1_out, controlled_buffer_1_out[0], controlled_buffer_1_out[1], controlled_buffer_1_out[2], controlled_buffer_1_out[3], controlled_buffer_1_out[4], controlled_buffer_1_out[5], controlled_buffer_1_out[6], controlled_buffer_1_out[7], controlled_buffer_1_out[8]);
  or or_2 (or_2_out, controlled_buffer_1_out[9], controlled_buffer_1_out[10], controlled_buffer_1_out[11], controlled_buffer_1_out[12], controlled_buffer_1_out[13], controlled_buffer_1_out[14], controlled_buffer_1_out[15]);
  nor nor_1 (Zero, or_1_out, or_2_out);

  // Notes on the sheet:
  //   Sergio Botero Uribe 20092
endmodule

module ALU2 (
  input  JZ,
  input  _0_AND_1_ADD,
  input  ALU_SIGNAL,
  input  [15:0] Num_1,
  input  [15:0] Num_2,
  output [15:0] Num_1___Num_2,
  output Overflow,
  output Zero
);

  wire and_1_out, and_18_out, and_19_out, not_2_out, not_3_out, or_1_out, or_2_out;
  wire [15:0] adder_1_out, adder_2_out, and_2_out, controlled_buffer_1_out, controlled_buffer_3_out,
       not_1_out;

  assign not_1_out = ~Num_2;  // NOT_Gate not_1, 16 bits wide
  Adder #(.width(16)) adder_1 (.a(not_1_out), .b(16'h1), .out(adder_1_out));  // open: cin, cout
  assign controlled_buffer_1_out = not_2_out ? Num_2 : 16'bz;  // Controlled_Buffer controlled_buffer_1
  not not_2 (not_2_out, and_1_out);
  assign controlled_buffer_1_out = and_1_out ? adder_1_out : 16'bz;  // Controlled_Buffer controlled_buffer_2
  and and_1 (and_1_out, JZ, _0_AND_1_ADD);
  Adder #(.width(16)) adder_2 (
    .a(Num_1), .b(controlled_buffer_1_out), .out(adder_2_out), .cout(Overflow));  // open: cin
  not not_3 (not_3_out, _0_AND_1_ADD);
  and and_2 (and_2_out[0], Num_1[0], controlled_buffer_1_out[0]);
  and and_3 (and_2_out[1], Num_1[1], controlled_buffer_1_out[1]);
  and and_4 (and_2_out[2], Num_1[2], controlled_buffer_1_out[2]);
  and and_5 (and_2_out[3], Num_1[3], controlled_buffer_1_out[3]);
  and and_6 (and_2_out[4], Num_1[4], controlled_buffer_1_out[4]);
  and and_7 (and_2_out[5], Num_1[5], controlled_buffer_1_out[5]);
  and and_8 (and_2_out[6], Num_1[6], controlled_buffer_1_out[6]);
  and and_9 (and_2_out[7], Num_1[7], controlled_buffer_1_out[7]);
  and and_10 (and_2_out[8], Num_1[8], controlled_buffer_1_out[8]);
  and and_11 (and_2_out[9], Num_1[9], controlled_buffer_1_out[9]);
  and and_12 (and_2_out[10], Num_1[10], controlled_buffer_1_out[10]);
  and and_13 (and_2_out[11], Num_1[11], controlled_buffer_1_out[11]);
  and and_14 (and_2_out[12], Num_1[12], controlled_buffer_1_out[12]);
  and and_15 (and_2_out[13], Num_1[13], controlled_buffer_1_out[13]);
  and and_16 (and_2_out[14], Num_1[14], controlled_buffer_1_out[14]);
  and and_17 (and_2_out[15], Num_1[15], controlled_buffer_1_out[15]);
  and and_18 (and_18_out, 1'b1, _0_AND_1_ADD);
  and and_19 (and_19_out, 1'b1, not_3_out);
  assign controlled_buffer_3_out = and_18_out ? adder_2_out : 16'bz;  // Controlled_Buffer controlled_buffer_3
  assign controlled_buffer_3_out = and_19_out ? and_2_out : 16'bz;  // Controlled_Buffer controlled_buffer_4
  assign Num_1___Num_2 = ALU_SIGNAL ? controlled_buffer_3_out : 16'bz;  // Controlled_Buffer controlled_buffer_5
  or or_1 (or_1_out, controlled_buffer_3_out[0], controlled_buffer_3_out[1], controlled_buffer_3_out[2], controlled_buffer_3_out[3], controlled_buffer_3_out[4], controlled_buffer_3_out[5], controlled_buffer_3_out[6], controlled_buffer_3_out[7], controlled_buffer_3_out[8]);
  or or_2 (or_2_out, controlled_buffer_3_out[9], controlled_buffer_3_out[10], controlled_buffer_3_out[11], controlled_buffer_3_out[12], controlled_buffer_3_out[13], controlled_buffer_3_out[14], controlled_buffer_3_out[15]);
  nor nor_1 (Zero, or_1_out, or_2_out);

  // Notes on the sheet:
  //   Sergio Botero Uribe 20092
endmodule

module REG (
  input  [15:0] In,
  input  W,
  input  R,
  input  [1:0] Num_Registro,
  output [15:0] Out_1,
  output [15:0] Out_2
);

  wire and_1_out, and_2_out, and_3_out, and_4_out, and_5_out, and_6_out, and_7_out, and_8_out, and_9_out,
       and_10_out, and_11_out, and_12_out, not_1_out, not_2_out, not_3_out, not_4_out;
  wire [15:0] controlled_buffer_1_out, controlled_buffer_3_out, controlled_buffer_6_out,
       controlled_buffer_7_out, Registro_1_q, Registro_2_q, Registro_3_q, Registro_4_q;

  assign controlled_buffer_1_out = and_1_out ? In : 16'bz;  // Controlled_Buffer controlled_buffer_1
  and and_1 (and_1_out, W, and_2_out);
  and and_2 (and_2_out, not_2_out, not_1_out);
  not not_1 (not_1_out, Num_Registro[1]);
  not not_2 (not_2_out, Num_Registro[0]);
  Controlled_Buffer #(.width(16)) controlled_buffer_2 (.in(Registro_1_q), .en(and_3_out));  // open: out
  Register #(.width(16), .trigger("high")) Registro_1 (
    .D(controlled_buffer_1_out), .Q(Registro_1_q), .clk(and_1_out));  // open: en, clr
  and and_3 (and_3_out, and_2_out, R);
  assign controlled_buffer_3_out = and_4_out ? In : 16'bz;  // Controlled_Buffer controlled_buffer_3
  and and_4 (and_4_out, W, and_5_out);
  and and_5 (and_5_out, Num_Registro[0], not_3_out);
  not not_3 (not_3_out, Num_Registro[1]);
  Controlled_Buffer #(.width(16)) controlled_buffer_4 (.in(Registro_2_q), .en(and_6_out));  // open: out
  Register #(.width(16), .trigger("high")) Registro_2 (
    .D(controlled_buffer_3_out), .Q(Registro_2_q), .clk(and_4_out));  // open: en, clr
  and and_6 (and_6_out, and_5_out, R);
  Controlled_Buffer #(.width(16)) controlled_buffer_5 (.in(Registro_3_q), .en(and_9_out));  // open: out
  Register #(.width(16), .trigger("high")) Registro_3 (
    .D(controlled_buffer_6_out), .Q(Registro_3_q), .clk(and_7_out));  // open: en, clr
  assign controlled_buffer_6_out = and_7_out ? In : 16'bz;  // Controlled_Buffer controlled_buffer_6
  and and_7 (and_7_out, W, and_8_out);
  and and_8 (and_8_out, not_4_out, Num_Registro[1]);
  not not_4 (not_4_out, Num_Registro[0]);
  and and_9 (and_9_out, and_8_out, R);
  assign controlled_buffer_7_out = and_10_out ? In : 16'bz;  // Controlled_Buffer controlled_buffer_7
  and and_10 (and_10_out, W, and_11_out);
  Controlled_Buffer #(.width(16)) controlled_buffer_8 (.in(Registro_4_q), .en(and_12_out));  // open: out
  Register #(.width(16), .trigger("high")) Registro_4 (
    .D(controlled_buffer_7_out), .Q(Registro_4_q), .clk(and_10_out));  // open: en, clr
  and and_11 (and_11_out, Num_Registro[0], Num_Registro[1]);
  and and_12 (and_12_out, and_11_out, R);

  // Notes on the sheet:
  //   Sergio Botero Uribe 20092
endmodule

module UC (
);

  ROM #(.addrWidth(16), .dataWidth(16)) rom_1 ();  // open: addr, data, sel

  // Notes on the sheet:
  //   Sergio Botero Uribe 20092
endmodule

module PROC (
);

  wire alu2_1_overflow, alu2_1_zero, clock_1_out, reg2_1_p1, reg2_1_p2, undriven, undriven_2, undriven_3,
       undriven_4, undriven_5, undriven_6, undriven_7;
  wire [1:0] reg2_1_p3;
  wire [15:0] adder_1_out, MAR_q, PC_q, ram_1_data, reg2_1_p4, reg2_1_p5;

  Clock #(.highDuration(1), .lowDuration(1)) clock_1 (.out(clock_1_out));
  Register #(.width(16), .trigger("high")) IR (.D(reg2_1_p4), .clk(undriven));  // open: en, Q, clr
  // REG2 reg2_1: pin names not known; wires that end beside it: reg2_1_p1, reg2_1_p2, reg2_1_p3, reg2_1_p4, reg2_1_p5
  ALU2 alu2_1 (
    .Num_1(reg2_1_p4), .Num_2(reg2_1_p5), ._0_AND_1_ADD(undriven_2), .ALU_SIGNAL(undriven_3),
    .Num_1___Num_2(reg2_1_p4), .Overflow(alu2_1_overflow), .Zero(alu2_1_zero));  // open: JZ
  Adder #(.width(16)) adder_1 (.a(PC_q), .b(16'h1), .out(adder_1_out));  // open: cin, cout
  Register #(.width(16), .trigger("high")) PC (.D(adder_1_out), .Q(PC_q), .clk(undriven_4));  // open: en, clr
  // Probe on alu2_1_overflow
  // Probe on alu2_1_zero
  Register #(.width(16), .trigger("high")) MAR (.D(PC_q), .Q(MAR_q), .clk(undriven_5));  // open: en, clr
  Register #(.width(16), .trigger("high")) MBR (.D(ram_1_data), .Q(reg2_1_p4), .clk(undriven_6));  // open: en, clr
  RAM #(.addrWidth(16), .dataWidth(16), .bus("combined")) ram_1 (
    .addr(MAR_q), .data(ram_1_data), .clk(undriven_7));  // open: sel, ld, clr

  // Notes on the sheet:
  //   REG
  //   ALU
  //   Dir
  //   Data
endmodule

module REG2 (
  input  [15:0] In,
  input  W,
  input  [1:0] Reg_W,
  input  [3:0] Reg_R_1___2,
  input  [1:0] R_bus,
  output [15:0] Out_Bus_1,
  output [15:0] Out_Bus_2
);

  wire and_1_out, and_2_out, and_3_out, and_4_out, and_5_out, and_6_out, and_7_out, and_8_out, and_9_out,
       and_10_out, and_11_out, and_12_out, not_1_out, not_2_out, not_3_out, not_4_out, not_5_out, not_6_out,
       not_7_out, not_8_out, not_9_out, not_10_out, not_11_out, not_12_out;
  wire [15:0] controlled_buffer_1_out, controlled_buffer_2_out, controlled_buffer_3_out, Registro_0_q,
       Registro_1_q, Registro_2_q, Registro_3_q;

  assign controlled_buffer_1_out = W ? In : 16'bz;  // Controlled_Buffer controlled_buffer_1
  not not_1 (not_1_out, Reg_W[0]);
  and and_1 (and_1_out, not_1_out, not_2_out);
  not not_2 (not_2_out, Reg_W[1]);
  not not_3 (not_3_out, Reg_W[1]);
  and and_2 (and_2_out, not_3_out, Reg_W[0]);
  and and_3 (and_3_out, Reg_W[1], not_4_out);
  not not_4 (not_4_out, Reg_W[0]);
  and and_4 (and_4_out, Reg_W[0], Reg_W[1]);
  Register #(.width(16), .trigger("high")) Registro_0 (
    .D(controlled_buffer_1_out), .Q(Registro_0_q), .clk(and_1_out));  // open: en, clr
  Register #(.width(16), .trigger("high")) Registro_1 (
    .D(controlled_buffer_1_out), .Q(Registro_1_q), .clk(and_2_out));  // open: en, clr
  Register #(.width(16), .trigger("high")) Registro_2 (
    .D(controlled_buffer_1_out), .Q(Registro_2_q), .clk(and_3_out));  // open: en, clr
  Register #(.width(16), .trigger("high")) Registro_3 (
    .D(controlled_buffer_1_out), .Q(Registro_3_q), .clk(and_4_out));  // open: en, clr
  not not_5 (not_5_out, Reg_R_1___2[0]);
  and and_5 (and_5_out, not_5_out, not_6_out);
  not not_6 (not_6_out, Reg_R_1___2[1]);
  not not_7 (not_7_out, Reg_R_1___2[3]);
  and and_6 (and_6_out, not_7_out, not_8_out);
  not not_8 (not_8_out, Reg_R_1___2[2]);
  not not_9 (not_9_out, Reg_R_1___2[1]);
  and and_7 (and_7_out, not_9_out, Reg_R_1___2[0]);
  not not_10 (not_10_out, Reg_R_1___2[3]);
  and and_8 (and_8_out, not_10_out, Reg_R_1___2[2]);
  and and_9 (and_9_out, Reg_R_1___2[1], not_11_out);
  not not_11 (not_11_out, Reg_R_1___2[0]);
  and and_10 (and_10_out, Reg_R_1___2[3], not_12_out);
  not not_12 (not_12_out, Reg_R_1___2[2]);
  and and_11 (and_11_out, Reg_R_1___2[0], Reg_R_1___2[1]);
  and and_12 (and_12_out, Reg_R_1___2[2], Reg_R_1___2[3]);
  assign controlled_buffer_2_out = and_5_out ? Registro_0_q : 16'bz;  // Controlled_Buffer controlled_buffer_2
  assign controlled_buffer_3_out = and_6_out ? Registro_0_q : 16'bz;  // Controlled_Buffer controlled_buffer_3
  assign controlled_buffer_2_out = and_7_out ? Registro_1_q : 16'bz;  // Controlled_Buffer controlled_buffer_4
  assign controlled_buffer_3_out = and_8_out ? Registro_1_q : 16'bz;  // Controlled_Buffer controlled_buffer_5
  assign controlled_buffer_2_out = and_9_out ? Registro_2_q : 16'bz;  // Controlled_Buffer controlled_buffer_6
  assign controlled_buffer_3_out = and_10_out ? Registro_2_q : 16'bz;  // Controlled_Buffer controlled_buffer_7
  assign controlled_buffer_2_out = and_11_out ? Registro_3_q : 16'bz;  // Controlled_Buffer controlled_buffer_8
  assign controlled_buffer_3_out = and_12_out ? Registro_3_q : 16'bz;  // Controlled_Buffer controlled_buffer_9
  assign Out_Bus_1 = R_bus[0] ? controlled_buffer_3_out : 16'bz;  // Controlled_Buffer controlled_buffer_10
  assign Out_Bus_2 = R_bus[1] ? controlled_buffer_2_out : 16'bz;  // Controlled_Buffer controlled_buffer_11
endmodule
