// Logisim project procesador st00254 estudiantes.circ as structural Verilog: 4 circuits, main circuit Procesador
module Procesador (
  input  [15:0] in_1,
  output [5:0] out_2
);

  wire [5:0] adder_1_out, register_1_q;
  wire [15:0] register_6_q;

  Register #(.width(6)) register_1 (.D(adder_1_out), .Q(register_1_q));  // open: en, clk, clr
  Register #(.width(16)) register_2 (.D(register_6_q));  // open: en, Q, clk, clr
  Register #(.width(16)) register_3 ();  // open: D, en, Q, clk, clr
  Register #(.width(16)) register_4 ();  // open: D, en, Q, clk, clr
  Adder #(.width(6)) adder_1 (.a(register_1_q), .b(6'b000001), .out(adder_1_out));  // open: cin, cout
  // Probe on register_1_q
  Register #(.width(6)) register_5 (.D(register_1_q), .Q(out_2));  // open: en, clk, clr
  Register #(.width(16)) register_6 (.D(in_1), .Q(register_6_q));  // open: en, clk, clr

  // Notes on the sheet:
  //   PC
  //   IR
  //   MAR
  //   MBR
endmodule

module ALU (
  input  [15:0] in_1,
  input  [15:0] in_2,
  output [15:0] out_3
);

  Adder #(.width(16)) adder_1 (.a(in_1), .b(in_2), .out(out_3));  // open: cin, cout
  AndBitaBit andbitabit_1 (
    .out_17(out_3[0]), .out_18(out_3[1]), .out_19(out_3[2]), .out_20(out_3[3]), .out_21(out_3[4]),
    .out_22(out_3[5]), .out_23(out_3[6]), .out_24(out_3[7]));  // open: in_1, in_2, in_3, in_4, in_5, in_6, in_7, in_8, in_9, in_10, in_11, in_12, in_13, in_14, in_15, in_16
  AndBitaBit andbitabit_2 (
    .out_17(out_3[8]), .out_18(out_3[9]), .out_19(out_3[10]), .out_20(out_3[11]), .out_21(out_3[12]),
    .out_22(out_3[13]), .out_23(out_3[14]), .out_24(out_3[15]));  // open: in_1, in_2, in_3, in_4, in_5, in_6, in_7, in_8, in_9, in_10, in_11, in_12, in_13, in_14, in_15, in_16
endmodule

module AndBitaBit (
  input  in_1,
  input  in_2,
  input  in_3,
  input  in_4,
  input  in_5,
  input  in_6,
  input  in_7,
  input  in_8,
  input  in_9,
  input  in_10,
  input  in_11,
  input  in_12,
  input  in_13,
  input  in_14,
  input  in_15,
  input  in_16,
  output out_17,
  output out_18,
  output out_19,
  output out_20,
  output out_21,
  output out_22,
  output out_23,
  output out_24
);

  and and_1 (out_17, in_1, in_2);
  and and_2 (out_18, in_3, in_4);
  and and_3 (out_19, in_5, in_6);
  and and_4 (out_20, in_7, in_8);
  and and_5 (out_21, in_9, in_10);
  and and_6 (out_22, in_11, in_12);
  and and_7 (out_23, in_13, in_14);
  and and_8 (out_24, in_15, in_16);
endmodule

module Board (
);

  wire undriven_2;
  wire [5:0] undriven;
  wire [7:0] ram_1_data;

  Procesador procesador_1 ();  // open: out_2, in_1
  RAM #(.addrWidth(6), .dataWidth(8)) ram_1 (
    .addr(undriven), .data(ram_1_data), .clk(undriven_2));  // open: sel, ld, clr

  // Notes on the sheet:
  //   Procesador
endmodule
