// Logisim project procesador st00254.circ as structural Verilog: 9 circuits, main circuit BoardJLMP
module ProcesadorJLMP (
  input  [15:0] DataToMBR,
  input  Clear,
  input  in_3,
  output [5:0] MARtoAddress,
  output [1:0] Control_Memoria
);

  wire alu_1_z, d_ff_1_q, uc_1_p18, uc_1_p21, uc_1_p22;
  wire [1:0] uc_1_p1, uc_1_p2, uc_1_p8;
  wire [4:0] uc_1_p20;
  wire [5:0] adder_1_out, multiplexer_2_out, multiplexer_5_out, register_6_q, register_7_q, uc_1_p13;
  wire [9:0] uc_1_p3;
  wire [15:0] alu_1_resultado, controlled_buffer_2_out, multiplexer_3_out, multiplexer_4_out, register_1_q,
       register_2_q, register_3_q, register_4_q, register_5_q, register_8_q, undriven;

  Multiplexer #(.select(2), .width(16)) multiplexer_1 (
    .in0(register_8_q), .in1(alu_1_resultado), .in2(controlled_buffer_2_out), .sel(uc_1_p8));  // open: in3, out
  Adder #(.width(6)) adder_1 (.a(register_6_q), .b(6'b000001), .out(adder_1_out));  // open: cin, cout
  Register #(.width(16), .trigger("rising")) register_1 (
    .D(undriven), .Q(register_1_q), .clk(uc_1_p3[0]), .clr(Clear));  // open: en
  Register #(.width(16), .trigger("rising")) register_2 (
    .D(undriven), .Q(register_2_q), .clk(uc_1_p3[1]), .clr(Clear));  // open: en
  Register #(.width(16), .trigger("rising")) register_3 (
    .D(undriven), .Q(register_3_q), .clk(uc_1_p3[2]), .clr(Clear));  // open: en
  Register #(.width(16), .trigger("rising")) register_4 (
    .D(undriven), .Q(register_4_q), .clk(uc_1_p3[3]), .clr(Clear));  // open: en
  Register #(.width(16), .trigger("rising")) register_5 (
    .D(undriven), .Q(register_5_q), .clk(uc_1_p3[4]), .clr(Clear));  // open: en
  // Probe on undriven
  Multiplexer #(.select(1), .width(6)) multiplexer_2 (
    .in0(adder_1_out), .in1(uc_1_p13), .out(multiplexer_2_out), .sel(uc_1_p20[4]));
  ALU alu_1 (.Resultado(alu_1_resultado), .OpAlu(uc_1_p3[9]), .Z(alu_1_z), .A(DataToMBR), .B(controlled_buffer_2_out));
  Register #(.width(6), .trigger("rising")) register_6 (
    .D(multiplexer_2_out), .Q(register_6_q), .clk(uc_1_p20[3]), .clr(Clear));  // open: en
  assign DataToMBR = uc_1_p3[8] ? multiplexer_3_out : 16'bz;  // Controlled_Buffer controlled_buffer_1
  Multiplexer #(.select(2), .width(16)) multiplexer_3 (
    .in0(register_2_q), .in1(register_3_q), .in2(register_4_q), .in3(register_5_q), .out(multiplexer_3_out),
    .sel(uc_1_p1));
  Multiplexer #(.select(2), .width(16)) multiplexer_4 (
    .in0(register_2_q), .in1(register_3_q), .in2(register_4_q), .in3(register_5_q), .out(multiplexer_4_out),
    .sel(uc_1_p2));
  assign controlled_buffer_2_out = uc_1_p3[7] ? multiplexer_4_out : 16'bz;  // Controlled_Buffer controlled_buffer_2
  Multiplexer #(.select(1), .width(6)) multiplexer_5 (
    .in0(register_6_q), .in1(uc_1_p13), .out(multiplexer_5_out), .sel(uc_1_p20[2]));
  D_Flip_Flop #(.trigger("rising")) d_ff_1 (.clk(uc_1_p18), .D(alu_1_z), .Q(d_ff_1_q));  // open: Qn, preset, en, reset
  Register #(.width(6), .trigger("rising")) register_7 (
    .D(multiplexer_5_out), .Q(register_7_q), .clk(uc_1_p20[1]), .clr(Clear));  // open: en
  Register #(.width(16), .trigger("high")) register_8 (
    .D(DataToMBR), .Q(register_8_q), .clk(uc_1_p21), .clr(Clear));  // open: en
  // UC uc_1: pin names not known; wires that end beside it: uc_1_p1, uc_1_p2, uc_1_p3[0], uc_1_p3[1], uc_1_p3[2], uc_1_p3[3], uc_1_p3[4], uc_1_p8, uc_1_p3[7], uc_1_p3[8], uc_1_p3[9], register_1_q, uc_1_p13, uc_1_p20[4], uc_1_p20[3], in_3, uc_1_p20[2], uc_1_p18, uc_1_p20[1], uc_1_p20[0], uc_1_p21, uc_1_p22, Control_Memoria[0], Control_Memoria[1]
  assign MARtoAddress = uc_1_p20[0] ? register_7_q : 6'bz;  // Controlled_Buffer controlled_buffer_3
  assign DataToMBR = uc_1_p22 ? register_8_q : 16'bz;  // Controlled_Buffer controlled_buffer_4

  // Notes on the sheet:
  //   IR
  //   PC
  //   MAR
endmodule

module BoardJLMP (
  input  Reset
);

  wire clock_1_out;
  wire [1:0] procesadorjlmp_1_control_memoria;
  wire [5:0] procesadorjlmp_1_martoaddress;
  wire [15:0] ram_1_data;

  ProcesadorJLMP procesadorjlmp_1 (
    .in_3(clock_1_out), .MARtoAddress(procesadorjlmp_1_martoaddress), .DataToMBR(ram_1_data),
    .Control_Memoria(procesadorjlmp_1_control_memoria), .Clear(Reset));
  Clock #(.highDuration(1), .lowDuration(1)) clock_1 (.out(clock_1_out));
  RAM #(.addrWidth(6), .dataWidth(16), .bus("combined")) ram_1 (
    .addr(procesadorjlmp_1_martoaddress), .data(ram_1_data), .clk(procesadorjlmp_1_control_memoria[1]),
    .ld(procesadorjlmp_1_control_memoria[0]));  // open: sel, clr
endmodule

module ALU (
  input  OpAlu,
  input  [15:0] A,
  input  [15:0] B,
  output [15:0] Resultado,
  output Z
);

  wire [7:0] andbitabit_1_out_3, andbitabit_2_out_3;
  wire [15:0] adder_1_out;

  Adder #(.width(16)) adder_1 (.a(A), .b(B), .out(adder_1_out));  // open: cin, cout
  AndBitaBit andbitabit_1 (
    .Parte_A(A[7:0]), .Parte_B(B[7:0]), .out_3(andbitabit_1_out_3[0]), .out_4(andbitabit_1_out_3[1]),
    .out_5(andbitabit_1_out_3[2]), .out_6(andbitabit_1_out_3[3]), .out_7(andbitabit_1_out_3[4]),
    .out_8(andbitabit_1_out_3[5]), .out_9(andbitabit_1_out_3[6]), .out_10(andbitabit_1_out_3[7]));
  AndBitaBit andbitabit_2 (
    .Parte_A(A[15:8]), .Parte_B(B[15:8]), .out_3(andbitabit_2_out_3[0]), .out_4(andbitabit_2_out_3[1]),
    .out_5(andbitabit_2_out_3[2]), .out_6(andbitabit_2_out_3[3]), .out_7(andbitabit_2_out_3[4]),
    .out_8(andbitabit_2_out_3[5]), .out_9(andbitabit_2_out_3[6]), .out_10(andbitabit_2_out_3[7]));
  Multiplexer #(.select(1), .width(16)) multiplexer_1 (
    .in0(adder_1_out), .in1({andbitabit_2_out_3, andbitabit_1_out_3}), .out(Resultado), .sel(OpAlu));
  Comparator #(.width(16), .mode("unsigned")) comparator_1 (.a(Resultado), .b({16{1'b0}}), .eq(Z));  // open: gt, lt
endmodule

module AndBitaBit (
  input  [7:0] Parte_A,
  input  [7:0] Parte_B,
  output out_3,
  output out_4,
  output out_5,
  output out_6,
  output out_7,
  output out_8,
  output out_9,
  output out_10
);

  and and_1 (out_3, Parte_A[0], Parte_B[0]);
  and and_2 (out_4, Parte_A[1], Parte_B[1]);
  and and_3 (out_5, Parte_A[2], Parte_B[2]);
  and and_4 (out_6, Parte_A[3], Parte_B[3]);
  and and_5 (out_7, Parte_A[4], Parte_B[4]);
  and and_6 (out_8, Parte_A[5], Parte_B[5]);
  and and_7 (out_9, Parte_A[6], Parte_B[6]);
  and and_8 (out_10, Parte_A[7], Parte_B[7]);
endmodule

module UC (
  input  [15:0] IR,
  input  Clock,
  input  Flag,
  output [5:0] out_4,
  output SelPCIn,
  output PCRegIn,
  output [1:0] Reg_0,
  output SelDirMar,
  output [1:0] Reg_1,
  output MARRegIn,
  output MARRegOut,
  output MDRRegIn,
  output MDRRegOutMem,
  output IRRegIn,
  output Reg0In,
  output Reg1In,
  output Reg2In,
  output Reg3In,
  output Read,
  output Write,
  output [1:0] SelBusC,
  output SelBusB,
  output SelBusA,
  output AluOp,
  output GrabarFlag
);

  wire decodeinstruccion_1_add, decodeinstruccion_1_movm, direccionmovm_1_memtoreg, direccionmovm_1_regtomem,
       or_2_out, tipodostres_1_out_3;
  wire [1:0] decodeinstruccion_1_and;
  wire [2:0] or_1_out;
  wire [7:0] adder_1_out, multiplexer_1_out, multiplexer_2_out, multiplexer_4_out, register_1_q, rom_1_data;
  wire [21:8] rom_1_data_2;

  DecodeInstruccion decodeinstruccion_1 (
    .Codigo_Operacion(IR[15:13]), .AluOp(AluOp), .ADD(decodeinstruccion_1_add),
    .AND(decodeinstruccion_1_and[0]), .MOVR(decodeinstruccion_1_and[1]), .MOVM(decodeinstruccion_1_movm),
    .JMP(or_1_out[1]), .JMPZ(or_1_out[2]));  // open: HALT, Error
  Adder #(.width(8)) adder_1 (.a(register_1_q), .b(8'h1), .out(adder_1_out));  // open: cin, cout
  Multiplexer #(.select(1), .width(8)) multiplexer_1 (
    .in0(adder_1_out), .in1(rom_1_data), .out(multiplexer_1_out), .sel(direccionmovm_1_memtoreg));
  Multiplexer #(.select(1), .width(8)) multiplexer_2 (
    .in0(adder_1_out), .in1(rom_1_data), .out(multiplexer_2_out), .sel(Flag));
  or or_1 (or_1_out[0], decodeinstruccion_1_add, decodeinstruccion_1_and[0], decodeinstruccion_1_and[1]);
  or or_2 (or_2_out, decodeinstruccion_1_and[0], decodeinstruccion_1_and[1]);
  Multiplexer #(.select(1), .width(2)) multiplexer_3 (
    .in0(IR[12:11]), .in1(IR[11:10]), .out(Reg_0), .sel(direccionmovm_1_regtomem));
  Multiplexer #(.select(3), .width(8)) multiplexer_4 (
    .in0(adder_1_out), .in1({1'b1, IR[15:13], 4'b0000}), .in3({8{1'b0}}), .in4(multiplexer_1_out),
    .in5(multiplexer_2_out), .out(multiplexer_4_out), .sel(rom_1_data_2[10:8]));  // open: in2, in6, in7
  and and_1 (GrabarFlag, or_2_out, rom_1_data_2[21]);
  DireccionMovM direccionmovm_1 (
    .RegToMem(direccionmovm_1_regtomem), .MemToReg(direccionmovm_1_memtoreg),
    .MOVM(decodeinstruccion_1_movm), .Direccion(IR[12]));
  Register #(.width(8), .trigger("rising")) register_1 (
    .D(multiplexer_4_out), .Q(register_1_q), .clk(Clock));  // open: en, clr
  assign out_4 = or_1_out[0] ? IR[12:7] : 6'bz;  // Controlled_Buffer controlled_buffer_1
  DecodeDestino decodedestino_1 (
    .Tipo1(or_1_out[0]), .JMP(or_1_out[1]), .JZ(or_1_out[2]), .Reg0(Reg0In), .Reg1(Reg1In), .Reg2(Reg2In),
    .Reg3(Reg3In), .RegDestOp1(IR[12:11]), .RegDestOp2(IR[11:10]), .RegIn(rom_1_data_2[21]));
  ROM #(.addrWidth(8), .dataWidth(26)) rom_1 (
    .addr(register_1_q),
    .data({SelBusA, SelBusB, SelBusC, rom_1_data_2[21], IRRegIn, SelPCIn, PCRegIn, SelDirMar, MARRegIn, MARRegOut, MDRRegIn, MDRRegOutMem, Write, Read, rom_1_data_2[10:8], rom_1_data}));  // open: sel
  assign out_4 = tipodostres_1_out_3 ? IR[9:4] : 6'bz;  // Controlled_Buffer controlled_buffer_2
  TipoDosTres tipodostres_1 (.JMP(or_1_out[1]), .JZ(or_1_out[2]), .out_3(tipodostres_1_out_3));

  assign Reg_1 = IR[10:9];

  // Notes on the sheet:
  //   Tipo 2
  //   Tipo 1
  //   Tipo 3
  //   contents of rom_1 (hex, n*v repeats v):
  //   4f800 18000 4800 46800 100100 123*0 700 15*0 3400000 3600300 14*0 3400000 3600300 14*0 1800000
  //   1a00300 14*0 20400 38000 4800 6800 100300 0 0 0 2020000 203a000 1000 1300 4*0 80000 c0300 14*0 80500
  //   300
endmodule

module DecodeInstruccion (
  input  [2:0] Codigo_Operacion,
  output HALT,
  output ADD,
  output AND,
  output MOVR,
  output MOVM,
  output JMP,
  output JMPZ,
  output Error,
  output AluOp
);

  wire not_1_out, or_1_out, or_2_out;

  Decoder #(.select(3), .tristate("false")) decoder_1 (
    .out0(HALT), .out1(ADD), .out2(AND), .out3(MOVR), .out4(MOVM), .out5(JMP), .out6(JMPZ), .out7(Error),
    .sel(Codigo_Operacion));
  not not_1 (not_1_out, ADD);
  or or_1 (or_1_out, ADD, AND);
  or or_2 (or_2_out, not_1_out, AND);
  assign AluOp = or_1_out ? or_2_out : 1'bz;  // Controlled_Buffer controlled_buffer_1
endmodule

module DecodeDestino (
  input  [1:0] RegDestOp1,
  input  [1:0] RegDestOp2,
  input  RegIn,
  input  Tipo1,
  input  JMP,
  input  JZ,
  output Reg0,
  output Reg1,
  output Reg2,
  output Reg3
);

  wire tipodostres_1_out_3;
  wire [3:0] controlled_buffer_1_out, decoder_1_out0, decoder_2_out0;

  Decoder #(.select(2), .tristate("false")) decoder_1 (
    .out0(decoder_1_out0[0]), .out1(decoder_1_out0[1]), .out2(decoder_1_out0[2]), .out3(decoder_1_out0[3]),
    .sel(RegDestOp1));
  Decoder #(.select(2), .tristate("false")) decoder_2 (
    .out0(decoder_2_out0[0]), .out1(decoder_2_out0[1]), .out2(decoder_2_out0[2]), .out3(decoder_2_out0[3]),
    .sel(RegDestOp2));
  TipoDosTres tipodostres_1 (.JMP(JMP), .JZ(JZ), .out_3(tipodostres_1_out_3));
  assign controlled_buffer_1_out = Tipo1 ? decoder_1_out0 : 4'bz;  // Controlled_Buffer controlled_buffer_1
  assign controlled_buffer_1_out = tipodostres_1_out_3 ? decoder_2_out0 : 4'bz;  // Controlled_Buffer controlled_buffer_2
  Multiplexer #(.select(1), .width(4)) multiplexer_1 (
    .in0(4'b0000), .in1(controlled_buffer_1_out), .out({Reg3, Reg2, Reg1, Reg0}), .sel(RegIn));
endmodule

module TipoDosTres (
  input  JMP,
  input  JZ,
  output out_3
);

  or or_1 (out_3, JMP, JZ);
endmodule

module DireccionMovM (
  input  MOVM,
  input  Direccion,
  output RegToMem,
  output MemToReg
);

  wire not_1_out;

  and and_1 (RegToMem, MOVM, Direccion);
  and and_2 (MemToReg, MOVM, not_1_out);
  not not_1 (not_1_out, Direccion);
endmodule
